# Fritzing sketch Pumpkin (saved by Fritzing 0.9.2b)

parts:
  J1 = Piezo Speaker
  J2 = Infrared Proximity Sensor  # not connected
  R1 = Resistor [resistance=220 tolerance=±5% package=THT]
  Arduino1 = Arduino Uno (Rev3)
  16K = Resistor [tolerance=±5% resistance=220 package=THT]  # not connected
  C1 = Electrolytic Capacitor [capacitance=1µF package="100 mil [THT, electrolytic]"]
  LED3 = LED - 5mm [color="Red (633nm)" package="5 mm [THT]"]
  LED2 = LED - 5mm [color="Yellow (585nm)" package="5 mm [THT]"]

nets:
  N1: J1.pin1, Arduino1.GND, C1.+, LED3.cathode, LED2.cathode
  N2: J1.pin2, Arduino1.D4
  N3: R1.Pin_1, LED3.anode, LED2.anode
  N4: Arduino1.A0, C1.-
